# Fritzing sketch Ordina IoT kijkdoos  (saved by Fritzing 0.9.3b)
breadboards: 1

parts:
  LED1 = RGB LED (com. cathode, rgb) [package="5 mm [THT]"]
  LED2 = LED - 5mm [color="Red (633nm)" package="5 mm [THT]"]
  LED3 = LED - 5mm [color="Red (633nm)" package="5 mm [THT]"]
  Onderdeel1 = Arduino Uno (Rev3)
  J1 = Basic Servo
  J2 = Piezo Speaker
  R1 = Resistor [tolerance=±5% resistance=330 package="0805 [SMD]"]
  R2 = Resistor [tolerance=±5% resistance=330 package="0805 [SMD]"]
  R5 = Resistor [tolerance=±5% resistance=220 package="0805 [SMD]"]
  R6 = Resistor [tolerance=±5% resistance=220 package="0805 [SMD]"]
  R7 = Resistor [tolerance=±5% resistance=220 package="0805 [SMD]"]
  Onderdeel2 = Bluetooth HM-10

nets:
  N1: LED1.red_anode, Onderdeel1.D6_PWM, R7.Pin_0, R7.Pin_1
  GND: LED1.common_cathode, LED2.cathode, LED3.cathode, Onderdeel1.GND, J1.gnd, J2.pin1, Onderdeel2.GND
  N2: LED1.green_anode, Onderdeel1.D5_PWM, R5.Pin_0, R5.Pin_1
  N3: LED1.blue_anode, Onderdeel1.D4, R6.Pin_0, R6.Pin_1
  N4: LED2.anode, Onderdeel1.D2, R2.Pin_0, R2.Pin_1
  N5: LED3.anode, Onderdeel1.D3_PWM, R1.Pin_0, R1.Pin_1
  N6: Onderdeel1.D8, J1.pulse
  N7: Onderdeel1.D10_PWM/SS, Onderdeel2.TXD
  N8: Onderdeel1.D11_PWM/MOSI, Onderdeel2.RXD
  N9: Onderdeel1.D7, J2.pin2
  3V3: Onderdeel1.3V3, Onderdeel2.VCC
  5V: Onderdeel1.5V, J1.vcc
